# Fritzing sketch curtains (saved by Fritzing 0.9.3b)
breadboards: 1

parts:
  Q1 = NPN-Transistor [package="TO92 [THT]"]
  Q2 = NPN-Transistor [package="TO92 [THT]"]
  Q4 = NPN-Transistor [package="TO92 [THT]"]
  Raspberry_Pi_1 = Raspberry Pi 3 [part_number=RPI-3-V1.2]
  Q5 = NPN-Transistor [package="TO92 [THT]"]
  S1 = Pushbutton [package="[THT]"]
  S2 = Pushbutton [package="[THT]"]
  R1 = Resistor [tolerance=±5% resistance=220 package=THT]
  LED1 = LED - 5mm [color="Red (633nm)" package="5 mm [THT]"]
  M1 = DC Motor

nets:
  N1: Q1.E, Q2.C, M1.pin_2
  N2: Q1.B, Raspberry_Pi_1.GIPO16
  N3: Q1.C, Q5.C, S1.Pin_3, S1.Pin_4, S2.Pin_3, S2.Pin_4, LED1.cathode
  N4: Q2.E, Q4.E
  N5: Q2.B, Raspberry_Pi_1.GIPO21
  N6: Q4.B, Raspberry_Pi_1.GIPO20
  N7: Q4.C, Q5.E, M1.pin_1
  N8: Raspberry_Pi_1.GIPO13, R1.Pin_1
  N9: Raspberry_Pi_1.GIPO19, S2.Pin_1, S2.Pin_2
  N10: Raspberry_Pi_1.GIPO26, S1.Pin_1, S1.Pin_2
  N11: Raspberry_Pi_1.GIPO12, Q5.B
  N12: R1.Pin_0, LED1.anode
