# Fritzing sketch rgbutton (saved by Fritzing 0.9.3b)
breadboards: 1

parts:
  LED1 = RGB LED (com. cathode, rgb) [package="5 mm [THT]"]
  S1 = Pushbutton [package="[THT]"]
  S2 = Pushbutton [package="[THT]"]
  S3 = Pushbutton [package="[THT]"]
  S4 = Pushbutton [package="[THT]"]
  Raspberry_Pi_1 = Raspberry Pi 3 [part_number=RPI-3-V1.2]
  R1 = Resistor [tolerance=±5% resistance=220 package=THT]
  R2 = Resistor [tolerance=±5% resistance=220 package=THT]
  R3 = Resistor [tolerance=±5% resistance=220 package=THT]

nets:
  N1: LED1.red_anode, R3.Pin_0
  N2: LED1.common_cathode, S1.Pin_1, S1.Pin_2, S2.Pin_1, S2.Pin_2, S3.Pin_1, S3.Pin_2, S4.Pin_1, S4.Pin_2
  N3: LED1.green_anode, R2.Pin_0
  N4: LED1.blue_anode, R1.Pin_0
  N5: S1.Pin_3, S1.Pin_4, Raspberry_Pi_1.GIPO12
  N6: S2.Pin_3, S2.Pin_4, Raspberry_Pi_1.GIPO16
  N7: S3.Pin_3, S3.Pin_4, Raspberry_Pi_1.GIPO20
  N8: S4.Pin_3, S4.Pin_4, Raspberry_Pi_1.GIPO21
  N9: Raspberry_Pi_1.GIPO13, R3.Pin_1
  N10: Raspberry_Pi_1.GIPO19, R2.Pin_1
  N11: Raspberry_Pi_1.GIPO26, R1.Pin_1
